# Fritzing sketch Frenar (saved by Fritzing 0.9.3b)

parts:
  Raspberry_Pi_1 = Raspberry Pi 3 [part_number=RPI-3-V1.2]
  U1 = MAX6675 [package=so08]
  U2 = MLX90614 [package=to-39]

nets:
  3V3: Raspberry_Pi_1.3v3, Raspberry_Pi_1.3V3, U1.VDD, U2.VDD
  N1: Raspberry_Pi_1.GPIO2, U2.PWM_SDA
  N2: Raspberry_Pi_1.GPIO3, U2.SCL_VZ
  N3: Raspberry_Pi_1.GIPO25, U1.SCK
  N4: Raspberry_Pi_1.GIPO24, U1.CS
  N5: Raspberry_Pi_1.GIPO18, U1.MISO
  GND: Raspberry_Pi_1.GND, U1.VSS

notes:
  CLK/SCK = GPIO25
  CS = GPIO24
  DO/SO/MISO = GPIO18
  VCC = 3.3V
  GND = GND
  SDA = GPIO2
  SCL = GPIO3
  VCC = 3.3V
  GND = GND
